# Fritzing sketch ControlMotores (saved by Fritzing 0.9.3b)

parts:
  S1 = H-Bridge with L298N
  Componente1 = Arduino Uno (Rev3)
  M1 = DC Motor
  M2 = DC Motor
  BAT1 = BC9VPC [package=bc9vpc]

nets:
  N1: S1.12V, BAT1.V+
  GND: S1.GND, Componente1.GND, BAT1.V-
  5V: S1.5V, Componente1.VIN
  N2: S1.IN1, Componente1.D13/SCK
  N3: S1.IN2, Componente1.D12/MISO
  N4: S1.IN3, Componente1.D11_PWM/MOSI
  N5: S1.IN4, Componente1.D10_PWM/SS
  N6: S1.ENB, Componente1.D9_PWM
  N7: S1.M1-01, M1.pin_2
  N8: S1.M1-02, M1.pin_1
  N9: S1.M2-01, M2.pin_2
  N10: S1.M2-02, M2.pin_1

custom parts:
  H-Bridge with L298N: h-bridge
