# Fritzing sketch RaspArduiUART (saved by Fritzing 0.9.3b)

parts:
  Raspberry_Pi_1 = Raspberry Pi 3 [part_number=RPI-3-V1.2]
  Componente1 = Logic Level Converter
  Componente2 = Arduino Uno (Rev3)

nets:
  N1: Raspberry_Pi_1.3v3, Componente1.LV
  GND: Raspberry_Pi_1.GND, Componente1.GND, Componente2.GND
  N2: Raspberry_Pi_1.GIPO15, Componente1.RX2_LV
  N3: Raspberry_Pi_1.GIPO14, Componente1.TX2_LV
  N4: Componente1.HV, Componente2.5V
  N5: Componente1.RX2_HV, Componente2.D1/TX
  N6: Componente1.TX2_HV, Componente2.D0/RX
